# Fritzing sketch Line follower wiring schematic (saved by Fritzing 0.9.6b)
breadboards: 1

parts:
  U1 = L9110 H-bridge module [part_number="L9110 H-bridge"]
  M1 = gear-motor [part_number="MOTOR LEFT"]
  M2 = gear-motor [part_number="MOTOR RIGHT"]
  Part1 = Arduino Uno (Rev3)
  BAT1 = BC9VPC [package=bc9vpc]
  VCC1 = 4 x AAA Battery Mount

nets:
  N1: U1.B-IA, Part1.D5_PWM
  N2: U1.B-IB, Part1.D4
  N3: U1.GND, VCC1.+
  N4: U1.VCC, VCC1.-
  N5: U1.A-IA, Part1.D3_PWM
  N6: U1.A-IB, Part1.D2
  N7: U1.MOTOR_A-A, M2.pin_2
  N8: U1.MOTOR_A-B, M2.pin_1
  N9: U1.MOTOR_B-A, M1.pin_1
  N10: U1.MOTOR_B-B, M1.pin_2
  N11: Part1.GND, BAT1.V-
  N12: Part1.VIN, BAT1.V+
